# Fritzing sketch Adapter (saved by Fritzing 0.9.3b)
circuit board: 2.4cm x 2.2cm

parts:
  J1 = female pin header, 6 pins [form="♀ (female)"]
  J2 = screw terminal, 6 pins

nets:
  N1: J1.pin1, J2.pin1
  N2: J1.pin2, J2.pin2
  N3: J1.pin3, J2.pin3
  N4: J1.pin4, J2.pin4
  N5: J1.pin5, J2.pin5
  N6: J1.pin6, J2.pin6
