# Fritzing sketch MotorControlPanel2 (saved by Fritzing 0.9.3b)
circuit board: 5.8cm x 2.2cm

parts:
  L9110 = IC, DIP package, 8 pins [chip_label=IC]
  atmega328 = atmega328 [package=dip]
  -+ = Battery
  R1 = Resistor [tolerance=±5% resistance=1 package=THT]
  R2 = Resistor [tolerance=±5% resistance=2 package=THT]
  M1_GND_C1_C2_VCC_M2 = female pin header, 6 pins [form="♀ (female)"]
  TX/RX = female pin header, 2 pins [form="♀ (female)"]
  TX/RX_2 = female pin header, 2 pins [form="♀ (female)"]
  -+_2 = Battery
  A+- = female pin header, 3 pins [form="♀ (female)"]
  R3 = Resistor [tolerance=±5% resistance=3 package=THT]

nets (from the pcb view):
  N1: L9110.pin1, M1_GND_C1_C2_VCC_M2.pin6
  N2: L9110.pin2, L9110.pin3, -+.+, R1.Pin_0, -+_2.+
  N3: L9110.pin4, M1_GND_C1_C2_VCC_M2.pin1
  N4: L9110.pin5, L9110.pin8, -+.-, R3.Pin_0
  N5: L9110.pin6, atmega328.D6_(PWM)
  N6: L9110.pin7, atmega328.D5_(PWM)
  N7: atmega328.VCC, R1.Pin_1, R2.Pin_1
  N8: atmega328.GND#7, R2.Pin_0, -+_2.-, R3.Pin_1
  N9: atmega328.D8, TX/RX.pin1
  N10: atmega328.D9_(PWM), TX/RX.pin2
  N11: atmega328.D10_(PWM), TX/RX_2.pin2
  N12: atmega328.D11_(PWM), TX/RX_2.pin1
  N13: atmega328.AREF, M1_GND_C1_C2_VCC_M2.pin5, A+-.pin2
  N14: atmega328.GND#21, M1_GND_C1_C2_VCC_M2.pin2, A+-.pin1
  N15: atmega328.A2, M1_GND_C1_C2_VCC_M2.pin4
  N16: atmega328.A3, M1_GND_C1_C2_VCC_M2.pin3
  N17: atmega328.A5, A+-.pin3
